// Logisim project logisim_Design.circ as structural Verilog: 4 circuits, main circuit main
module main (
  input  [7:0] multiplier,
  input  [7:0] Multiplicand,
  output [15:0] out_3
);

  wire adder_1_cout, adder_2_cout, adder_2_out, adder_3_cout, adder_3_out, adder_4_cout, adder_4_out,
       adder_5_cout, adder_5_out, adder_6_cout, adder_6_out, adder_7_cout, adder_7_out, adder_8_cout,
       adder_8_out, adder_9_cout, adder_10_cout, adder_10_out, adder_11_cout, adder_11_out, adder_12_cout,
       adder_12_out, adder_13_cout, adder_13_out, adder_14_cout, adder_14_out, adder_15_cout, adder_15_out,
       adder_16_cout, adder_16_out, adder_17_cout, adder_18_cout, adder_18_out, adder_19_cout, adder_19_out,
       adder_20_cout, adder_20_out, adder_21_cout, adder_21_out, adder_22_cout, adder_22_out, adder_23_cout,
       adder_23_out, adder_24_cout, adder_24_out, adder_25_cout, adder_26_cout, adder_26_out, adder_27_cout,
       adder_27_out, adder_28_cout, adder_28_out, adder_29_cout, adder_29_out, adder_30_cout, adder_30_out,
       adder_31_cout, adder_31_out, adder_32_cout, adder_32_out, adder_33_cout, adder_34_cout, adder_34_out,
       adder_35_cout, adder_35_out, adder_36_cout, adder_36_out, adder_37_cout, adder_37_out, adder_38_cout,
       adder_38_out, adder_39_cout, adder_39_out, adder_40_cout, adder_40_out, adder_41_cout, adder_42_cout,
       adder_42_out, adder_43_cout, adder_43_out, adder_44_cout, adder_44_out, adder_45_cout, adder_45_out,
       adder_46_cout, adder_46_out, adder_47_cout, adder_47_out, adder_48_cout, adder_48_out, adder_49_cout,
       adder_50_cout, adder_50_out, adder_51_cout, adder_51_out, adder_52_cout, adder_52_out, adder_53_cout,
       adder_53_out, adder_54_cout, adder_54_out, adder_55_cout, adder_55_out, adder_56_cout, adder_56_out,
       adder_57_cout, adder_58_cout, adder_59_cout, adder_60_cout, adder_61_cout, adder_62_cout,
       adder_63_cout, adder_64_cout, and_2_out, and_3_out, and_4_out, and_5_out, and_6_out, and_7_out,
       and_8_out, and_9_out, and_10_out, and_11_out, and_12_out, and_13_out, and_14_out, and_15_out,
       and_16_out, and_17_out, and_18_out, and_19_out, and_20_out, and_21_out, and_22_out, and_23_out,
       and_24_out, and_25_out, and_26_out, and_27_out, and_28_out, and_29_out, and_30_out, and_31_out,
       and_32_out, and_33_out, and_34_out, and_35_out, and_36_out, and_37_out, and_38_out, and_39_out,
       and_40_out, and_41_out, and_42_out, and_43_out, and_44_out, and_45_out, and_46_out, and_47_out,
       and_48_out, and_49_out, and_50_out, and_51_out, and_52_out, and_53_out, and_54_out, and_55_out,
       and_56_out, and_57_out, and_58_out, and_59_out, and_60_out, and_61_out, and_62_out, and_63_out,
       and_64_out, and_65_out, and_66_out, and_67_out, and_68_out, and_69_out, and_70_out, and_71_out,
       and_72_out, bin_2_bcd_16_1_out_2, bin_2_bcd_16_1_out_3, bin_2_bcd_16_1_out_4, bin_2_bcd_16_1_out_5,
       bin_2_bcd_16_1_out_6, bin_2_bcd_16_1_out_7, bin_2_bcd_16_1_out_8, bin_2_bcd_16_1_out_9,
       bin_2_bcd_16_1_out_10, bin_2_bcd_16_1_out_11, bin_2_bcd_16_1_out_12, bin_2_bcd_16_1_out_13,
       n4_bit_decoder_7seg_2_a_2, n4_bit_decoder_7seg_2_b_2, n4_bit_decoder_7seg_2_c_2,
       n4_bit_decoder_7seg_2_d_2, n4_bit_decoder_7seg_2_e, n4_bit_decoder_7seg_2_f, n4_bit_decoder_7seg_2_g,
       n4_bit_decoder_7seg_3_a_2, n4_bit_decoder_7seg_3_b_2, n4_bit_decoder_7seg_3_c_2,
       n4_bit_decoder_7seg_3_d_2, n4_bit_decoder_7seg_3_e, n4_bit_decoder_7seg_3_f, n4_bit_decoder_7seg_3_g,
       n4_bit_decoder_7seg_4_a_2, n4_bit_decoder_7seg_4_b_2, n4_bit_decoder_7seg_4_c_2,
       n4_bit_decoder_7seg_4_d_2, n4_bit_decoder_7seg_4_e, n4_bit_decoder_7seg_4_f, n4_bit_decoder_7seg_4_g,
       undriven;

  and and_1 (out_3[0], Multiplicand[0], multiplier[0]);
  and and_2 (and_2_out, Multiplicand[1], multiplier[0]);
  and and_3 (and_3_out, Multiplicand[2], multiplier[0]);
  and and_4 (and_4_out, Multiplicand[3], multiplier[0]);
  and and_5 (and_5_out, Multiplicand[4], multiplier[0]);
  and and_6 (and_6_out, Multiplicand[5], multiplier[0]);
  and and_7 (and_7_out, Multiplicand[6], multiplier[0]);
  and and_8 (and_8_out, Multiplicand[7], multiplier[0]);
  and and_9 (and_9_out, Multiplicand[0], multiplier[1]);
  and and_10 (and_10_out, Multiplicand[1], multiplier[1]);
  and and_11 (and_11_out, Multiplicand[2], multiplier[1]);
  and and_12 (and_12_out, Multiplicand[3], multiplier[1]);
  and and_13 (and_13_out, Multiplicand[4], multiplier[1]);
  and and_14 (and_14_out, Multiplicand[5], multiplier[1]);
  and and_15 (and_15_out, Multiplicand[6], multiplier[1]);
  and and_16 (and_16_out, Multiplicand[7], multiplier[1]);
  Adder #(.width(1)) adder_1 (.a(and_2_out), .b(and_9_out), .out(out_3[1]), .cin(1'b0), .cout(adder_1_cout));
  Adder #(.width(1)) adder_2 (
    .a(and_3_out), .b(and_10_out), .out(adder_2_out), .cin(adder_1_cout), .cout(adder_2_cout));
  Adder #(.width(1)) adder_3 (
    .a(and_4_out), .b(and_11_out), .out(adder_3_out), .cin(adder_2_cout), .cout(adder_3_cout));
  Adder #(.width(1)) adder_4 (
    .a(and_5_out), .b(and_12_out), .out(adder_4_out), .cin(adder_3_cout), .cout(adder_4_cout));
  Adder #(.width(1)) adder_5 (
    .a(and_6_out), .b(and_13_out), .out(adder_5_out), .cin(adder_4_cout), .cout(adder_5_cout));
  Adder #(.width(1)) adder_6 (
    .a(and_7_out), .b(and_14_out), .out(adder_6_out), .cin(adder_5_cout), .cout(adder_6_cout));
  Adder #(.width(1)) adder_7 (
    .a(and_8_out), .b(and_15_out), .out(adder_7_out), .cin(adder_6_cout), .cout(adder_7_cout));
  Adder #(.width(1)) adder_8 (.a(adder_7_cout), .b(and_16_out), .out(adder_8_out), .cin(1'b0), .cout(adder_8_cout));
  and and_17 (and_17_out, Multiplicand[0], multiplier[2]);
  and and_18 (and_18_out, Multiplicand[1], multiplier[2]);
  and and_19 (and_19_out, Multiplicand[2], multiplier[2]);
  and and_20 (and_20_out, Multiplicand[3], multiplier[2]);
  and and_21 (and_21_out, Multiplicand[4], multiplier[2]);
  and and_22 (and_22_out, Multiplicand[5], multiplier[2]);
  and and_23 (and_23_out, Multiplicand[6], multiplier[2]);
  and and_24 (and_24_out, Multiplicand[7], multiplier[2]);
  Adder #(.width(1)) adder_9 (.a(adder_2_out), .b(and_17_out), .out(out_3[2]), .cin(1'b0), .cout(adder_9_cout));
  Adder #(.width(1)) adder_10 (
    .a(adder_3_out), .b(and_18_out), .out(adder_10_out), .cin(adder_9_cout), .cout(adder_10_cout));
  Adder #(.width(1)) adder_11 (
    .a(adder_4_out), .b(and_19_out), .out(adder_11_out), .cin(adder_10_cout), .cout(adder_11_cout));
  Adder #(.width(1)) adder_12 (
    .a(adder_5_out), .b(and_20_out), .out(adder_12_out), .cin(adder_11_cout), .cout(adder_12_cout));
  Adder #(.width(1)) adder_13 (
    .a(adder_6_out), .b(and_21_out), .out(adder_13_out), .cin(adder_12_cout), .cout(adder_13_cout));
  Adder #(.width(1)) adder_14 (
    .a(adder_7_out), .b(and_22_out), .out(adder_14_out), .cin(adder_13_cout), .cout(adder_14_cout));
  Adder #(.width(1)) adder_15 (
    .a(adder_8_out), .b(and_23_out), .out(adder_15_out), .cin(adder_14_cout), .cout(adder_15_cout));
  Adder #(.width(1)) adder_16 (
    .a(adder_8_cout), .b(and_24_out), .out(adder_16_out), .cin(adder_15_cout), .cout(adder_16_cout));
  and and_25 (and_25_out, Multiplicand[0], multiplier[3]);
  and and_26 (and_26_out, Multiplicand[1], multiplier[3]);
  and and_27 (and_27_out, Multiplicand[2], multiplier[3]);
  and and_28 (and_28_out, Multiplicand[3], multiplier[3]);
  and and_29 (and_29_out, Multiplicand[4], multiplier[3]);
  and and_30 (and_30_out, Multiplicand[5], multiplier[3]);
  and and_31 (and_31_out, Multiplicand[6], multiplier[3]);
  and and_32 (and_32_out, Multiplicand[7], multiplier[3]);
  Adder #(.width(1)) adder_17 (.a(adder_10_out), .b(and_25_out), .out(out_3[3]), .cin(1'b0), .cout(adder_17_cout));
  Adder #(.width(1)) adder_18 (
    .a(adder_11_out), .b(and_26_out), .out(adder_18_out), .cin(adder_17_cout), .cout(adder_18_cout));
  Adder #(.width(1)) adder_19 (
    .a(adder_12_out), .b(and_27_out), .out(adder_19_out), .cin(adder_18_cout), .cout(adder_19_cout));
  Adder #(.width(1)) adder_20 (
    .a(adder_13_out), .b(and_28_out), .out(adder_20_out), .cin(adder_19_cout), .cout(adder_20_cout));
  Adder #(.width(1)) adder_21 (
    .a(adder_14_out), .b(and_29_out), .out(adder_21_out), .cin(adder_20_cout), .cout(adder_21_cout));
  Adder #(.width(1)) adder_22 (
    .a(adder_15_out), .b(and_30_out), .out(adder_22_out), .cin(adder_21_cout), .cout(adder_22_cout));
  Adder #(.width(1)) adder_23 (
    .a(adder_16_out), .b(and_31_out), .out(adder_23_out), .cin(adder_22_cout), .cout(adder_23_cout));
  Adder #(.width(1)) adder_24 (
    .a(adder_16_cout), .b(and_32_out), .out(adder_24_out), .cin(adder_23_cout), .cout(adder_24_cout));
  and and_33 (and_33_out, Multiplicand[0], multiplier[4]);
  and and_34 (and_34_out, Multiplicand[1], multiplier[4]);
  and and_35 (and_35_out, Multiplicand[2], multiplier[4]);
  and and_36 (and_36_out, Multiplicand[3], multiplier[4]);
  and and_37 (and_37_out, Multiplicand[4], multiplier[4]);
  and and_38 (and_38_out, Multiplicand[5], multiplier[4]);
  and and_39 (and_39_out, Multiplicand[6], multiplier[4]);
  and and_40 (and_40_out, Multiplicand[7], multiplier[4]);
  Adder #(.width(1)) adder_25 (.a(adder_18_out), .b(and_33_out), .out(out_3[4]), .cin(1'b0), .cout(adder_25_cout));
  Adder #(.width(1)) adder_26 (
    .a(adder_19_out), .b(and_34_out), .out(adder_26_out), .cin(adder_25_cout), .cout(adder_26_cout));
  Adder #(.width(1)) adder_27 (
    .a(adder_20_out), .b(and_35_out), .out(adder_27_out), .cin(adder_26_cout), .cout(adder_27_cout));
  Adder #(.width(1)) adder_28 (
    .a(adder_21_out), .b(and_36_out), .out(adder_28_out), .cin(adder_27_cout), .cout(adder_28_cout));
  Adder #(.width(1)) adder_29 (
    .a(adder_22_out), .b(and_37_out), .out(adder_29_out), .cin(adder_28_cout), .cout(adder_29_cout));
  Adder #(.width(1)) adder_30 (
    .a(adder_23_out), .b(and_38_out), .out(adder_30_out), .cin(adder_29_cout), .cout(adder_30_cout));
  Adder #(.width(1)) adder_31 (
    .a(adder_24_out), .b(and_39_out), .out(adder_31_out), .cin(adder_30_cout), .cout(adder_31_cout));
  Adder #(.width(1)) adder_32 (
    .a(adder_24_cout), .b(and_40_out), .out(adder_32_out), .cin(adder_31_cout), .cout(adder_32_cout));
  and and_41 (and_41_out, Multiplicand[0], multiplier[5]);
  and and_42 (and_42_out, Multiplicand[1], multiplier[5]);
  and and_43 (and_43_out, Multiplicand[2], multiplier[5]);
  and and_44 (and_44_out, Multiplicand[3], multiplier[5]);
  and and_45 (and_45_out, Multiplicand[4], multiplier[5]);
  and and_46 (and_46_out, Multiplicand[5], multiplier[5]);
  and and_47 (and_47_out, Multiplicand[6], multiplier[5]);
  and and_48 (and_48_out, Multiplicand[7], multiplier[5]);
  _4_bit_decoder_7seg u_4_bit_decoder_7seg_1 ();  // open: A, B, C, D, a_2, b_2, c_2, d_2, e, f, g
  Adder #(.width(1)) adder_33 (.a(adder_26_out), .b(and_41_out), .out(out_3[5]), .cin(1'b0), .cout(adder_33_cout));
  Adder #(.width(1)) adder_34 (
    .a(adder_27_out), .b(and_42_out), .out(adder_34_out), .cin(adder_33_cout), .cout(adder_34_cout));
  Adder #(.width(1)) adder_35 (
    .a(adder_28_out), .b(and_43_out), .out(adder_35_out), .cin(adder_34_cout), .cout(adder_35_cout));
  Adder #(.width(1)) adder_36 (
    .a(adder_29_out), .b(and_44_out), .out(adder_36_out), .cin(adder_35_cout), .cout(adder_36_cout));
  Adder #(.width(1)) adder_37 (
    .a(adder_30_out), .b(and_45_out), .out(adder_37_out), .cin(adder_36_cout), .cout(adder_37_cout));
  Adder #(.width(1)) adder_38 (
    .a(adder_31_out), .b(and_46_out), .out(adder_38_out), .cin(adder_37_cout), .cout(adder_38_cout));
  Adder #(.width(1)) adder_39 (
    .a(adder_32_out), .b(and_47_out), .out(adder_39_out), .cin(adder_38_cout), .cout(adder_39_cout));
  Adder #(.width(1)) adder_40 (
    .a(adder_32_cout), .b(and_48_out), .out(adder_40_out), .cin(adder_39_cout), .cout(adder_40_cout));
  BIN_2_BCD_16 bin_2_bcd_16_1 (
    .in_1(out_3), .out_2(bin_2_bcd_16_1_out_2), .out_3(bin_2_bcd_16_1_out_3), .out_4(bin_2_bcd_16_1_out_4),
    .out_5(bin_2_bcd_16_1_out_5), .out_6(bin_2_bcd_16_1_out_6), .out_7(bin_2_bcd_16_1_out_7),
    .out_8(bin_2_bcd_16_1_out_8), .out_9(bin_2_bcd_16_1_out_9), .out_10(bin_2_bcd_16_1_out_10),
    .out_11(bin_2_bcd_16_1_out_11), .out_12(bin_2_bcd_16_1_out_12), .out_13(bin_2_bcd_16_1_out_13));
  and and_49 (and_49_out, Multiplicand[0], multiplier[6]);
  and and_50 (and_50_out, Multiplicand[1], multiplier[6]);
  and and_51 (and_51_out, Multiplicand[2], multiplier[6]);
  and and_52 (and_52_out, Multiplicand[3], multiplier[6]);
  and and_53 (and_53_out, Multiplicand[4], multiplier[6]);
  and and_54 (and_54_out, Multiplicand[5], multiplier[6]);
  and and_55 (and_55_out, Multiplicand[6], multiplier[6]);
  and and_56 (and_56_out, Multiplicand[7], multiplier[6]);
  _7_Segment_Display u_7_segment_display_1 (.g(adder_64_cout), .f(undriven));  // open: a, b, e, d, c, dp
  Adder #(.width(1)) adder_41 (.a(adder_34_out), .b(and_49_out), .out(out_3[6]), .cin(1'b0), .cout(adder_41_cout));
  Adder #(.width(1)) adder_42 (
    .a(adder_35_out), .b(and_50_out), .out(adder_42_out), .cin(adder_41_cout), .cout(adder_42_cout));
  Adder #(.width(1)) adder_43 (
    .a(adder_36_out), .b(and_51_out), .out(adder_43_out), .cin(adder_42_cout), .cout(adder_43_cout));
  Adder #(.width(1)) adder_44 (
    .a(adder_37_out), .b(and_52_out), .out(adder_44_out), .cin(adder_43_cout), .cout(adder_44_cout));
  Adder #(.width(1)) adder_45 (
    .a(adder_38_out), .b(and_53_out), .out(adder_45_out), .cin(adder_44_cout), .cout(adder_45_cout));
  Adder #(.width(1)) adder_46 (
    .a(adder_39_out), .b(and_54_out), .out(adder_46_out), .cin(adder_45_cout), .cout(adder_46_cout));
  Adder #(.width(1)) adder_47 (
    .a(adder_40_out), .b(and_55_out), .out(adder_47_out), .cin(adder_46_cout), .cout(adder_47_cout));
  Adder #(.width(1)) adder_48 (
    .a(adder_40_cout), .b(and_56_out), .out(adder_48_out), .cin(adder_47_cout), .cout(adder_48_cout));
  _4_bit_decoder_7seg u_4_bit_decoder_7seg_2 (
    .A(bin_2_bcd_16_1_out_5), .B(bin_2_bcd_16_1_out_4), .C(bin_2_bcd_16_1_out_3), .D(bin_2_bcd_16_1_out_2),
    .a_2(n4_bit_decoder_7seg_2_a_2), .b_2(n4_bit_decoder_7seg_2_b_2), .c_2(n4_bit_decoder_7seg_2_c_2),
    .d_2(n4_bit_decoder_7seg_2_d_2), .e(n4_bit_decoder_7seg_2_e), .f(n4_bit_decoder_7seg_2_f),
    .g(n4_bit_decoder_7seg_2_g));
  _7_Segment_Display u_7_segment_display_2 (
    .g(n4_bit_decoder_7seg_2_g), .f(n4_bit_decoder_7seg_2_f), .a(n4_bit_decoder_7seg_2_a_2),
    .b(n4_bit_decoder_7seg_2_b_2), .e(n4_bit_decoder_7seg_2_e), .d(n4_bit_decoder_7seg_2_d_2),
    .c(n4_bit_decoder_7seg_2_c_2));  // open: dp
  and and_57 (and_57_out, Multiplicand[0], multiplier[6]);
  and and_58 (and_58_out, Multiplicand[1], multiplier[6]);
  and and_59 (and_59_out, Multiplicand[2], multiplier[6]);
  and and_60 (and_60_out, Multiplicand[3], multiplier[6]);
  and and_61 (and_61_out, Multiplicand[4], multiplier[6]);
  and and_62 (and_62_out, Multiplicand[5], multiplier[6]);
  and and_63 (and_63_out, Multiplicand[6], multiplier[6]);
  and and_64 (and_64_out, Multiplicand[7], multiplier[6]);
  Adder #(.width(1)) adder_49 (.a(adder_42_out), .b(and_57_out), .out(out_3[7]), .cin(1'b0), .cout(adder_49_cout));
  Adder #(.width(1)) adder_50 (
    .a(adder_43_out), .b(and_58_out), .out(adder_50_out), .cin(adder_49_cout), .cout(adder_50_cout));
  Adder #(.width(1)) adder_51 (
    .a(adder_44_out), .b(and_59_out), .out(adder_51_out), .cin(adder_50_cout), .cout(adder_51_cout));
  Adder #(.width(1)) adder_52 (
    .a(adder_45_out), .b(and_60_out), .out(adder_52_out), .cin(adder_51_cout), .cout(adder_52_cout));
  Adder #(.width(1)) adder_53 (
    .a(adder_46_out), .b(and_61_out), .out(adder_53_out), .cin(adder_52_cout), .cout(adder_53_cout));
  Adder #(.width(1)) adder_54 (
    .a(adder_47_out), .b(and_62_out), .out(adder_54_out), .cin(adder_53_cout), .cout(adder_54_cout));
  Adder #(.width(1)) adder_55 (
    .a(adder_48_out), .b(and_63_out), .out(adder_55_out), .cin(adder_54_cout), .cout(adder_55_cout));
  Adder #(.width(1)) adder_56 (
    .a(adder_48_cout), .b(and_64_out), .out(adder_56_out), .cin(adder_55_cout), .cout(adder_56_cout));
  _4_bit_decoder_7seg u_4_bit_decoder_7seg_3 (
    .A(bin_2_bcd_16_1_out_9), .B(bin_2_bcd_16_1_out_8), .C(bin_2_bcd_16_1_out_7), .D(bin_2_bcd_16_1_out_6),
    .a_2(n4_bit_decoder_7seg_3_a_2), .b_2(n4_bit_decoder_7seg_3_b_2), .c_2(n4_bit_decoder_7seg_3_c_2),
    .d_2(n4_bit_decoder_7seg_3_d_2), .e(n4_bit_decoder_7seg_3_e), .f(n4_bit_decoder_7seg_3_f),
    .g(n4_bit_decoder_7seg_3_g));
  _7_Segment_Display u_7_segment_display_3 (
    .g(n4_bit_decoder_7seg_3_g), .f(n4_bit_decoder_7seg_3_f), .a(n4_bit_decoder_7seg_3_a_2),
    .b(n4_bit_decoder_7seg_3_b_2), .e(n4_bit_decoder_7seg_3_e), .d(n4_bit_decoder_7seg_3_d_2),
    .c(n4_bit_decoder_7seg_3_c_2));  // open: dp
  and and_65 (and_65_out, Multiplicand[0], multiplier[7]);
  and and_66 (and_66_out, Multiplicand[1], multiplier[7]);
  and and_67 (and_67_out, Multiplicand[2], multiplier[7]);
  and and_68 (and_68_out, Multiplicand[3], multiplier[7]);
  and and_69 (and_69_out, Multiplicand[4], multiplier[7]);
  and and_70 (and_70_out, Multiplicand[5], multiplier[7]);
  and and_71 (and_71_out, Multiplicand[6], multiplier[7]);
  and and_72 (and_72_out, Multiplicand[7], multiplier[7]);
  Adder #(.width(1)) adder_57 (.a(adder_50_out), .b(and_65_out), .out(out_3[8]), .cin(1'b0), .cout(adder_57_cout));
  Adder #(.width(1)) adder_58 (
    .a(adder_51_out), .b(and_66_out), .out(out_3[9]), .cin(adder_57_cout), .cout(adder_58_cout));
  Adder #(.width(1)) adder_59 (
    .a(adder_52_out), .b(and_67_out), .out(out_3[10]), .cin(adder_58_cout), .cout(adder_59_cout));
  Adder #(.width(1)) adder_60 (
    .a(adder_53_out), .b(and_68_out), .out(out_3[11]), .cin(adder_59_cout), .cout(adder_60_cout));
  Adder #(.width(1)) adder_61 (
    .a(adder_54_out), .b(and_69_out), .out(out_3[12]), .cin(adder_60_cout), .cout(adder_61_cout));
  Adder #(.width(1)) adder_62 (
    .a(adder_55_out), .b(and_70_out), .out(out_3[13]), .cin(adder_61_cout), .cout(adder_62_cout));
  Adder #(.width(1)) adder_63 (
    .a(adder_56_out), .b(and_71_out), .out(out_3[14]), .cin(adder_62_cout), .cout(adder_63_cout));
  Adder #(.width(1)) adder_64 (
    .a(adder_56_cout), .b(and_72_out), .out(out_3[15]), .cin(adder_63_cout), .cout(adder_64_cout));
  _4_bit_decoder_7seg u_4_bit_decoder_7seg_4 (
    .A(bin_2_bcd_16_1_out_13), .B(bin_2_bcd_16_1_out_12), .C(bin_2_bcd_16_1_out_11),
    .D(bin_2_bcd_16_1_out_10), .a_2(n4_bit_decoder_7seg_4_a_2), .b_2(n4_bit_decoder_7seg_4_b_2),
    .c_2(n4_bit_decoder_7seg_4_c_2), .d_2(n4_bit_decoder_7seg_4_d_2), .e(n4_bit_decoder_7seg_4_e),
    .f(n4_bit_decoder_7seg_4_f), .g(n4_bit_decoder_7seg_4_g));
  _7_Segment_Display u_7_segment_display_4 (
    .g(n4_bit_decoder_7seg_4_g), .f(n4_bit_decoder_7seg_4_f), .a(n4_bit_decoder_7seg_4_a_2),
    .b(n4_bit_decoder_7seg_4_b_2), .e(n4_bit_decoder_7seg_4_e), .d(n4_bit_decoder_7seg_4_d_2),
    .c(n4_bit_decoder_7seg_4_c_2));  // open: dp

  // Other names for the same wires on the sheet: y0 = Multiplicand[0]; y1 = Multiplicand[1]; y2 = Multiplicand[2];
  //   y3 = Multiplicand[3]; y4 = Multiplicand[4]; y5 = Multiplicand[5]; y6 = Multiplicand[6]; y7 = Multiplicand[7];
  //   x0 = multiplier[0]; x1 = multiplier[1]; x2 = multiplier[2]; x3 = multiplier[3]; x4 = multiplier[4];
  //   x5 = multiplier[5]; x6 = multiplier[6]; x7 = multiplier[7]
endmodule

// d
module _4_bit_decoder_7seg (
  input  A,
  input  B,
  input  C,
  input  D,
  output a_2,
  output b_2,
  output c_2,
  output d_2,
  output e,
  output f,
  output g
);

  wire and_1_out, and_2_out, and_3_out, and_4_out, and_5_out, and_6_out, and_7_out, and_8_out, and_9_out,
       and_10_out, and_11_out, and_12_out, and_13_out, and_14_out, and_15_out, and_16_out, not_1_out,
       not_2_out, not_3_out, not_4_out, not_5_out, not_6_out, not_7_out, not_8_out, not_9_out, not_10_out,
       not_11_out, not_12_out, not_13_out, not_14_out, not_15_out, not_16_out, not_17_out, not_18_out,
       not_19_out, not_20_out, not_21_out;

  not not_1 (not_1_out, C);
  and and_1 (and_1_out, not_1_out, not_2_out);
  not not_2 (not_2_out, A);
  and and_2 (and_2_out, C, A);
  not not_3 (not_3_out, C);
  not not_4 (not_4_out, B);
  and and_3 (and_3_out, not_4_out, not_5_out);
  not not_5 (not_5_out, A);
  and and_4 (and_4_out, B, A);
  or or_1 (c_2, C, not_6_out, A);
  not not_6 (not_6_out, B);
  not not_7 (not_7_out, C);
  and and_5 (and_5_out, not_7_out, not_8_out);
  not not_8 (not_8_out, A);
  and and_6 (and_6_out, B, not_9_out);
  not not_9 (not_9_out, A);
  and and_7 (and_7_out, C, not_10_out, A);
  not not_10 (not_10_out, B);
  not not_11 (not_11_out, C);
  and and_8 (and_8_out, not_11_out, B);
  not not_12 (not_12_out, C);
  and and_9 (and_9_out, not_12_out, not_13_out);
  not not_13 (not_13_out, A);
  and and_10 (and_10_out, B, not_14_out);
  not not_14 (not_14_out, A);
  not not_15 (not_15_out, B);
  and and_11 (and_11_out, not_15_out, not_16_out);
  not not_16 (not_16_out, A);
  and and_12 (and_12_out, C, not_17_out);
  not not_17 (not_17_out, B);
  and and_13 (and_13_out, C, not_18_out);
  not not_18 (not_18_out, A);
  and and_14 (and_14_out, C, not_19_out);
  not not_19 (not_19_out, B);
  not not_20 (not_20_out, C);
  and and_15 (and_15_out, not_20_out, B);
  and and_16 (and_16_out, B, not_21_out);
  not not_21 (not_21_out, A);
  or or_2 (a_2, and_1_out, B, and_2_out, D);
  or or_3 (b_2, not_3_out, and_3_out, and_4_out);
  or or_4 (d_2, and_5_out, and_6_out, and_7_out, and_8_out, D);
  or or_5 (e, and_9_out, and_10_out);
  or or_6 (f, D, and_11_out, and_12_out, and_13_out);
  or or_7 (g, D, and_14_out, and_15_out, and_16_out);
endmodule

module BCD (
  input  Pin_8,
  input  Pin_4,
  input  Pin_2,
  input  pin_1,
  input  Cin,
  output Cout,
  output BCD_8,
  output BCD_4,
  output BCD_2,
  output BCD_1
);

  wire adder_2_cout, adder_3_cout, adder_4_cout, and_1_out, or_1_out, or_2_out;

  and and_1 (and_1_out, Pin_4, or_2_out);
  or or_1 (or_1_out, and_1_out, Pin_8);
  or or_2 (or_2_out, pin_1, Pin_2);
  Adder #(.width(1)) adder_1 (.a(Pin_8), .b(adder_4_cout), .out(Cout));  // open: cin, cout
  Adder #(.width(1)) adder_2 (.a(Pin_2), .b(or_1_out), .out(BCD_4), .cin(adder_3_cout), .cout(adder_2_cout));
  Adder #(.width(1)) adder_3 (.a(pin_1), .b(or_1_out), .out(BCD_2), .cout(adder_3_cout));  // open: cin
  Adder #(.width(1)) adder_4 (.a(Pin_4), .b(adder_2_cout), .out(BCD_8), .cout(adder_4_cout));  // open: cin

  assign BCD_1 = Cin;
endmodule

module BIN_2_BCD_16 (
  input  [15:0] in_1,
  output out_2,
  output out_3,
  output out_4,
  output out_5,
  output out_6,
  output out_7,
  output out_8,
  output out_9,
  output out_10,
  output out_11,
  output out_12,
  output out_13
);

  wire bcd_1_bcd_1, bcd_1_bcd_2, bcd_1_bcd_4, bcd_1_bcd_8, bcd_2_bcd_1, bcd_2_bcd_2, bcd_2_bcd_4,
       bcd_2_bcd_8, bcd_3_bcd_1, bcd_3_bcd_2, bcd_3_bcd_4, bcd_3_bcd_8, bcd_3_cout, bcd_4_bcd_1, bcd_4_bcd_2,
       bcd_4_bcd_4, bcd_4_bcd_8, bcd_4_cout, bcd_5_bcd_1, bcd_5_bcd_2, bcd_5_bcd_4, bcd_5_bcd_8, bcd_6_bcd_1,
       bcd_6_bcd_2, bcd_6_bcd_4, bcd_6_bcd_8, bcd_7_bcd_1, bcd_7_bcd_2, bcd_7_bcd_4, bcd_7_bcd_8, bcd_7_cout,
       bcd_8_bcd_1, bcd_8_bcd_2, bcd_8_bcd_4, bcd_8_bcd_8, bcd_8_cout, bcd_9_bcd_1, bcd_9_bcd_2, bcd_9_bcd_4,
       bcd_9_bcd_8, bcd_9_cout, bcd_10_bcd_1, bcd_10_bcd_2, bcd_10_bcd_4, bcd_10_bcd_8, bcd_10_cout,
       bcd_11_bcd_1, bcd_11_bcd_2, bcd_11_bcd_4, bcd_11_bcd_8, bcd_11_cout, bcd_12_bcd_1, bcd_12_bcd_2,
       bcd_12_bcd_4, bcd_12_bcd_8, bcd_13_bcd_1, bcd_13_bcd_2, bcd_13_bcd_4, bcd_13_bcd_8, bcd_14_bcd_1,
       bcd_14_bcd_2, bcd_14_bcd_4, bcd_14_bcd_8, bcd_14_cout, bcd_15_bcd_1, bcd_15_bcd_2, bcd_15_bcd_4,
       bcd_15_bcd_8, bcd_15_cout, bcd_16_bcd_1, bcd_16_bcd_2, bcd_16_bcd_4, bcd_16_bcd_8, bcd_16_cout,
       bcd_17_bcd_1, bcd_17_bcd_2, bcd_17_bcd_4, bcd_17_bcd_8, bcd_17_cout, bcd_18_bcd_1, bcd_18_bcd_2,
       bcd_18_bcd_4, bcd_18_bcd_8, bcd_19_bcd_1, bcd_19_bcd_2, bcd_19_bcd_4, bcd_19_bcd_8, bcd_20_bcd_1,
       bcd_20_bcd_2, bcd_20_bcd_4, bcd_20_bcd_8, bcd_21_bcd_1, bcd_21_bcd_2, bcd_21_bcd_4, bcd_21_bcd_8,
       bcd_21_cout, bcd_22_bcd_1, bcd_22_bcd_2, bcd_22_bcd_4, bcd_22_bcd_8, bcd_22_cout, bcd_23_bcd_1,
       bcd_23_bcd_2, bcd_23_bcd_4, bcd_23_bcd_8, bcd_23_cout, bcd_24_bcd_1, bcd_24_bcd_2, bcd_24_bcd_4,
       bcd_24_bcd_8, bcd_24_cout, bcd_25_bcd_1, bcd_25_bcd_2, bcd_25_bcd_4, bcd_25_bcd_8, bcd_25_cout,
       bcd_26_bcd_1, bcd_26_bcd_2, bcd_26_bcd_4, bcd_26_bcd_8, bcd_26_cout, bcd_27_bcd_1, bcd_27_bcd_2,
       bcd_27_bcd_4, bcd_27_bcd_8, bcd_28_bcd_1, bcd_28_bcd_2, bcd_28_bcd_4, bcd_28_bcd_8, bcd_30_bcd_1,
       bcd_30_bcd_2, bcd_30_bcd_4, bcd_30_bcd_8, bcd_30_cout, bcd_31_cout, bcd_32_bcd_1, bcd_32_bcd_2,
       bcd_32_bcd_4, bcd_32_bcd_8, bcd_32_cout, bcd_33_bcd_1, bcd_33_bcd_2, bcd_33_bcd_4, bcd_33_bcd_8,
       bcd_33_cout, bcd_34_bcd_1, bcd_34_bcd_2, bcd_34_bcd_4, bcd_34_bcd_8, bcd_34_cout, bcd_35_cout;

  BCD bcd_1 (
    .Pin_8(1'b0), .Pin_4(1'b0), .Pin_2(1'b0), .pin_1(bcd_4_cout), .Cin(bcd_3_cout), .BCD_8(bcd_1_bcd_8),
    .BCD_4(bcd_1_bcd_4), .BCD_2(bcd_1_bcd_2), .BCD_1(bcd_1_bcd_1));  // open: Cout
  BCD bcd_2 (
    .Pin_8(1'b0), .Pin_4(1'b0), .Pin_2(in_1[15]), .pin_1(in_1[14]), .Cin(in_1[13]), .BCD_8(bcd_2_bcd_8),
    .BCD_4(bcd_2_bcd_4), .BCD_2(bcd_2_bcd_2), .BCD_1(bcd_2_bcd_1));  // open: Cout
  BCD bcd_3 (
    .Pin_8(bcd_4_bcd_8), .Pin_4(bcd_4_bcd_4), .Pin_2(bcd_4_bcd_2), .pin_1(bcd_4_bcd_1), .Cout(bcd_3_cout),
    .Cin(in_1[11]), .BCD_8(bcd_3_bcd_8), .BCD_4(bcd_3_bcd_4), .BCD_2(bcd_3_bcd_2), .BCD_1(bcd_3_bcd_1));
  BCD bcd_4 (
    .Pin_8(bcd_2_bcd_8), .Pin_4(bcd_2_bcd_4), .Pin_2(bcd_2_bcd_2), .pin_1(bcd_2_bcd_1), .Cout(bcd_4_cout),
    .Cin(in_1[12]), .BCD_8(bcd_4_bcd_8), .BCD_4(bcd_4_bcd_4), .BCD_2(bcd_4_bcd_2), .BCD_1(bcd_4_bcd_1));
  BCD bcd_5 (
    .Pin_8(1'b0), .Pin_4(1'b0), .Pin_2(1'b0), .pin_1(bcd_8_cout), .Cin(bcd_7_cout), .BCD_8(bcd_5_bcd_8),
    .BCD_4(bcd_5_bcd_4), .BCD_2(bcd_5_bcd_2), .BCD_1(bcd_5_bcd_1));  // open: Cout
  BCD bcd_6 (
    .Pin_8(bcd_1_bcd_8), .Pin_4(bcd_1_bcd_4), .Pin_2(bcd_1_bcd_2), .pin_1(bcd_1_bcd_1), .Cin(bcd_11_cout),
    .BCD_8(bcd_6_bcd_8), .BCD_4(bcd_6_bcd_4), .BCD_2(bcd_6_bcd_2), .BCD_1(bcd_6_bcd_1));  // open: Cout
  BCD bcd_7 (
    .Pin_8(bcd_8_bcd_8), .Pin_4(bcd_8_bcd_4), .Pin_2(bcd_8_bcd_2), .pin_1(bcd_8_bcd_1), .Cout(bcd_7_cout),
    .Cin(bcd_9_cout), .BCD_8(bcd_7_bcd_8), .BCD_4(bcd_7_bcd_4), .BCD_2(bcd_7_bcd_2), .BCD_1(bcd_7_bcd_1));
  BCD bcd_8 (
    .Pin_8(bcd_6_bcd_8), .Pin_4(bcd_6_bcd_4), .Pin_2(bcd_6_bcd_2), .pin_1(bcd_6_bcd_1), .Cout(bcd_8_cout),
    .Cin(bcd_10_cout), .BCD_8(bcd_8_bcd_8), .BCD_4(bcd_8_bcd_4), .BCD_2(bcd_8_bcd_2), .BCD_1(bcd_8_bcd_1));
  BCD bcd_9 (
    .Pin_8(bcd_10_bcd_8), .Pin_4(bcd_10_bcd_4), .Pin_2(bcd_10_bcd_2), .pin_1(bcd_10_bcd_1),
    .Cout(bcd_9_cout), .Cin(in_1[8]), .BCD_8(bcd_9_bcd_8), .BCD_4(bcd_9_bcd_4), .BCD_2(bcd_9_bcd_2),
    .BCD_1(bcd_9_bcd_1));
  BCD bcd_10 (
    .Pin_8(bcd_11_bcd_8), .Pin_4(bcd_11_bcd_4), .Pin_2(bcd_11_bcd_2), .pin_1(bcd_11_bcd_1),
    .Cout(bcd_10_cout), .Cin(in_1[9]), .BCD_8(bcd_10_bcd_8), .BCD_4(bcd_10_bcd_4), .BCD_2(bcd_10_bcd_2),
    .BCD_1(bcd_10_bcd_1));
  BCD bcd_11 (
    .Pin_8(bcd_3_bcd_8), .Pin_4(bcd_3_bcd_4), .Pin_2(bcd_3_bcd_2), .pin_1(bcd_3_bcd_1), .Cout(bcd_11_cout),
    .Cin(in_1[10]), .BCD_8(bcd_11_bcd_8), .BCD_4(bcd_11_bcd_4), .BCD_2(bcd_11_bcd_2), .BCD_1(bcd_11_bcd_1));
  BCD bcd_12 (
    .Pin_8(bcd_13_bcd_8), .Pin_4(bcd_13_bcd_4), .Pin_2(bcd_13_bcd_2), .pin_1(bcd_13_bcd_1),
    .Cin(bcd_15_cout), .BCD_8(bcd_12_bcd_8), .BCD_4(bcd_12_bcd_4), .BCD_2(bcd_12_bcd_2), .BCD_1(bcd_12_bcd_1));  // open: Cout
  BCD bcd_13 (
    .Pin_8(bcd_5_bcd_8), .Pin_4(bcd_5_bcd_4), .Pin_2(bcd_5_bcd_2), .pin_1(bcd_5_bcd_1), .Cin(bcd_14_cout),
    .BCD_8(bcd_13_bcd_8), .BCD_4(bcd_13_bcd_4), .BCD_2(bcd_13_bcd_2), .BCD_1(bcd_13_bcd_1));  // open: Cout
  BCD bcd_14 (
    .Pin_8(bcd_7_bcd_8), .Pin_4(bcd_7_bcd_4), .Pin_2(bcd_7_bcd_2), .pin_1(bcd_7_bcd_1), .Cout(bcd_14_cout),
    .Cin(bcd_17_cout), .BCD_8(bcd_14_bcd_8), .BCD_4(bcd_14_bcd_4), .BCD_2(bcd_14_bcd_2), .BCD_1(bcd_14_bcd_1));
  BCD bcd_15 (
    .Pin_8(bcd_14_bcd_8), .Pin_4(bcd_14_bcd_4), .Pin_2(bcd_14_bcd_2), .pin_1(bcd_14_bcd_1),
    .Cout(bcd_15_cout), .Cin(bcd_16_cout), .BCD_8(bcd_15_bcd_8), .BCD_4(bcd_15_bcd_4), .BCD_2(bcd_15_bcd_2),
    .BCD_1(bcd_15_bcd_1));
  BCD bcd_16 (
    .Pin_8(bcd_17_bcd_8), .Pin_4(bcd_17_bcd_4), .Pin_2(bcd_17_bcd_2), .pin_1(bcd_17_bcd_1),
    .Cout(bcd_16_cout), .Cin(in_1[6]), .BCD_8(bcd_16_bcd_8), .BCD_4(bcd_16_bcd_4), .BCD_2(bcd_16_bcd_2),
    .BCD_1(bcd_16_bcd_1));
  BCD bcd_17 (
    .Pin_8(bcd_9_bcd_8), .Pin_4(bcd_9_bcd_4), .Pin_2(bcd_9_bcd_2), .pin_1(bcd_9_bcd_1), .Cout(bcd_17_cout),
    .Cin(in_1[7]), .BCD_8(bcd_17_bcd_8), .BCD_4(bcd_17_bcd_4), .BCD_2(bcd_17_bcd_2), .BCD_1(bcd_17_bcd_1));
  BCD bcd_18 (
    .Pin_8(bcd_19_bcd_8), .Pin_4(bcd_19_bcd_4), .Pin_2(bcd_19_bcd_2), .pin_1(bcd_19_bcd_1),
    .Cin(bcd_21_cout), .BCD_8(bcd_18_bcd_8), .BCD_4(bcd_18_bcd_4), .BCD_2(bcd_18_bcd_2), .BCD_1(bcd_18_bcd_1));  // open: Cout
  BCD bcd_19 (
    .Pin_8(bcd_12_bcd_8), .Pin_4(bcd_12_bcd_4), .Pin_2(bcd_12_bcd_2), .pin_1(bcd_12_bcd_1),
    .Cin(bcd_23_cout), .BCD_8(bcd_19_bcd_8), .BCD_4(bcd_19_bcd_4), .BCD_2(bcd_19_bcd_2), .BCD_1(bcd_19_bcd_1));  // open: Cout
  BCD bcd_20 (
    .Pin_8(bcd_18_bcd_8), .Pin_4(bcd_18_bcd_4), .Pin_2(bcd_18_bcd_2), .pin_1(bcd_18_bcd_1),
    .Cin(bcd_22_cout), .BCD_8(bcd_20_bcd_8), .BCD_4(bcd_20_bcd_4), .BCD_2(bcd_20_bcd_2), .BCD_1(bcd_20_bcd_1));  // open: Cout
  BCD bcd_21 (
    .Pin_8(bcd_23_bcd_8), .Pin_4(bcd_23_bcd_4), .Pin_2(bcd_23_bcd_2), .pin_1(bcd_23_bcd_1),
    .Cout(bcd_21_cout), .Cin(bcd_24_cout), .BCD_8(bcd_21_bcd_8), .BCD_4(bcd_21_bcd_4), .BCD_2(bcd_21_bcd_2),
    .BCD_1(bcd_21_bcd_1));
  BCD bcd_22 (
    .Pin_8(bcd_21_bcd_8), .Pin_4(bcd_21_bcd_4), .Pin_2(bcd_21_bcd_2), .pin_1(bcd_21_bcd_1),
    .Cout(bcd_22_cout), .Cin(bcd_26_cout), .BCD_8(bcd_22_bcd_8), .BCD_4(bcd_22_bcd_4), .BCD_2(bcd_22_bcd_2),
    .BCD_1(bcd_22_bcd_1));
  BCD bcd_23 (
    .Pin_8(bcd_15_bcd_8), .Pin_4(bcd_15_bcd_4), .Pin_2(bcd_15_bcd_2), .pin_1(bcd_15_bcd_1),
    .Cout(bcd_23_cout), .Cin(bcd_25_cout), .BCD_8(bcd_23_bcd_8), .BCD_4(bcd_23_bcd_4), .BCD_2(bcd_23_bcd_2),
    .BCD_1(bcd_23_bcd_1));
  BCD bcd_24 (
    .Pin_8(bcd_25_bcd_8), .Pin_4(bcd_25_bcd_4), .Pin_2(bcd_25_bcd_2), .pin_1(bcd_25_bcd_1),
    .Cout(bcd_24_cout), .Cin(in_1[4]), .BCD_8(bcd_24_bcd_8), .BCD_4(bcd_24_bcd_4), .BCD_2(bcd_24_bcd_2),
    .BCD_1(bcd_24_bcd_1));
  BCD bcd_25 (
    .Pin_8(bcd_16_bcd_8), .Pin_4(bcd_16_bcd_4), .Pin_2(bcd_16_bcd_2), .pin_1(bcd_16_bcd_1),
    .Cout(bcd_25_cout), .Cin(in_1[5]), .BCD_8(bcd_25_bcd_8), .BCD_4(bcd_25_bcd_4), .BCD_2(bcd_25_bcd_2),
    .BCD_1(bcd_25_bcd_1));
  BCD bcd_26 (
    .Pin_8(bcd_24_bcd_8), .Pin_4(bcd_24_bcd_4), .Pin_2(bcd_24_bcd_2), .pin_1(bcd_24_bcd_1),
    .Cout(bcd_26_cout), .Cin(in_1[3]), .BCD_8(bcd_26_bcd_8), .BCD_4(bcd_26_bcd_4), .BCD_2(bcd_26_bcd_2),
    .BCD_1(bcd_26_bcd_1));
  BCD bcd_27 (
    .Pin_8(bcd_20_bcd_8), .Pin_4(bcd_20_bcd_4), .Pin_2(bcd_20_bcd_2), .pin_1(bcd_20_bcd_1),
    .Cin(bcd_30_cout), .BCD_8(bcd_27_bcd_8), .BCD_4(bcd_27_bcd_4), .BCD_2(bcd_27_bcd_2), .BCD_1(bcd_27_bcd_1));  // open: Cout
  BCD bcd_28 (
    .Pin_8(bcd_27_bcd_8), .Pin_4(bcd_27_bcd_4), .Pin_2(bcd_27_bcd_2), .pin_1(bcd_27_bcd_1),
    .Cin(bcd_32_cout), .BCD_8(bcd_28_bcd_8), .BCD_4(bcd_28_bcd_4), .BCD_2(bcd_28_bcd_2), .BCD_1(bcd_28_bcd_1));  // open: Cout
  BCD bcd_29 (
    .Pin_8(bcd_28_bcd_8), .Pin_4(bcd_28_bcd_4), .Pin_2(bcd_28_bcd_2), .pin_1(bcd_28_bcd_1),
    .Cin(bcd_31_cout), .BCD_8(out_2), .BCD_4(out_3), .BCD_2(out_4), .BCD_1(out_5));  // open: Cout
  BCD bcd_30 (
    .Pin_8(bcd_22_bcd_8), .Pin_4(bcd_22_bcd_4), .Pin_2(bcd_22_bcd_2), .pin_1(bcd_22_bcd_1),
    .Cout(bcd_30_cout), .Cin(bcd_34_cout), .BCD_8(bcd_30_bcd_8), .BCD_4(bcd_30_bcd_4), .BCD_2(bcd_30_bcd_2),
    .BCD_1(bcd_30_bcd_1));
  BCD bcd_31 (
    .Pin_8(bcd_32_bcd_8), .Pin_4(bcd_32_bcd_4), .Pin_2(bcd_32_bcd_2), .pin_1(bcd_32_bcd_1),
    .Cout(bcd_31_cout), .Cin(bcd_35_cout), .BCD_8(out_6), .BCD_4(out_7), .BCD_2(out_8), .BCD_1(out_9));
  BCD bcd_32 (
    .Pin_8(bcd_30_bcd_8), .Pin_4(bcd_30_bcd_4), .Pin_2(bcd_30_bcd_2), .pin_1(bcd_30_bcd_1),
    .Cout(bcd_32_cout), .Cin(bcd_33_cout), .BCD_8(bcd_32_bcd_8), .BCD_4(bcd_32_bcd_4), .BCD_2(bcd_32_bcd_2),
    .BCD_1(bcd_32_bcd_1));
  BCD bcd_33 (
    .Pin_8(bcd_34_bcd_8), .Pin_4(bcd_34_bcd_4), .Pin_2(bcd_34_bcd_2), .pin_1(bcd_34_bcd_1),
    .Cout(bcd_33_cout), .Cin(in_1[1]), .BCD_8(bcd_33_bcd_8), .BCD_4(bcd_33_bcd_4), .BCD_2(bcd_33_bcd_2),
    .BCD_1(bcd_33_bcd_1));
  BCD bcd_34 (
    .Pin_8(bcd_26_bcd_8), .Pin_4(bcd_26_bcd_4), .Pin_2(bcd_26_bcd_2), .pin_1(bcd_26_bcd_1),
    .Cout(bcd_34_cout), .Cin(in_1[2]), .BCD_8(bcd_34_bcd_8), .BCD_4(bcd_34_bcd_4), .BCD_2(bcd_34_bcd_2),
    .BCD_1(bcd_34_bcd_1));
  BCD bcd_35 (
    .Pin_8(bcd_33_bcd_8), .Pin_4(bcd_33_bcd_4), .Pin_2(bcd_33_bcd_2), .pin_1(bcd_33_bcd_1),
    .Cout(bcd_35_cout), .Cin(in_1[0]), .BCD_8(out_10), .BCD_4(out_11), .BCD_2(out_12), .BCD_1(out_13));
endmodule
